# Fritzing sketch Poolbuddy wiring (saved by Fritzing 0.9.3b)
breadboards: 1

parts:
  Part1 = Photon
  pH_Circuit1 = pH Circuit
  ORP_Circuit1 = ORP Circuit
  Pre-Assembled_Female_BNC1 = Pre-Assembled Female BNC
  Pre-Assembled_Female_BNC2 = Pre-Assembled Female BNC
  DS1 = DS18B20 1-Wire Temperature Sensor [part_number=DS18B20]
  D1 = Schottky Diode [part_number=1N5817 package="300 mil [THT]"]
  IC1 = Voltage Regulator [package=78xxl]
  R1 = Resistor [tolerance=±5% resistance=220 package="0603 [SMD]"]
  D2 = SOLAR-IXYS [package=solarbit-12x1]  # not connected

nets:
  GND: Part1.GND, pH_Circuit1.GND#0, ORP_Circuit1.GND#0, DS1.GND, IC1.GND
  N1: Part1.VIN, IC1.OUT
  N2: Part1.D0, pH_Circuit1.TX
  N3: Part1.D1, pH_Circuit1.RX
  N4: Part1.D5, DS1.DQ, R1.Pin_0
  VCC: Part1.D6, pH_Circuit1.Vcc, ORP_Circuit1.Vcc, Pre-Assembled_Female_BNC1.NC, Pre-Assembled_Female_BNC2.NC, DS1.VDD, R1.Pin_1
  N5: pH_Circuit1.PRB, Pre-Assembled_Female_BNC1.PRB
  N6: pH_Circuit1.GND#5, Pre-Assembled_Female_BNC1.GND
  N7: ORP_Circuit1.PRB, Pre-Assembled_Female_BNC2.PRB
  N8: ORP_Circuit1.GND#5, Pre-Assembled_Female_BNC2.GND
  N9: D1.cathode, IC1.IN
