# Fritzing sketch Poolbuddy2 (saved by Fritzing 0.9.8b)
breadboards: 1

parts:
  pH_Circuit1 = pH Circuit
  ORP_Circuit1 = ORP Circuit
  Pre-Assembled_Female_BNC1 = Pre-Assembled Female BNC
  Pre-Assembled_Female_BNC2 = Pre-Assembled Female BNC
  DS1 = DS18B20 1-Wire Temperature Sensor [part_number=DS18B20]
  R1 = Resistor [tolerance=±5% resistance=220 package="0603 [SMD]"]
  Argon1 = Particle Argon

nets:
  GND: pH_Circuit1.GND#0, ORP_Circuit1.GND#0, DS1.GND, Argon1.GND
  N1: pH_Circuit1.TX, Argon1.SDA
  N2: pH_Circuit1.RX, Argon1.SCL
  N3: pH_Circuit1.Vcc, Pre-Assembled_Female_BNC1.NC, R1.Pin_1, Argon1.RESET
  N4: pH_Circuit1.PRB, Pre-Assembled_Female_BNC1.PRB
  N5: pH_Circuit1.GND#5, Pre-Assembled_Female_BNC1.GND
  N6: ORP_Circuit1.Vcc, Pre-Assembled_Female_BNC2.NC
  N7: ORP_Circuit1.PRB, Pre-Assembled_Female_BNC2.PRB
  N8: ORP_Circuit1.GND#5, Pre-Assembled_Female_BNC2.GND
  N9: DS1.DQ, R1.Pin_0, Argon1.A5
  N10: DS1.VDD, Argon1.A2

custom parts:
  Particle Argon: The Argon is a powerful Wi-Fi enabled development board that can act as either a standalone Wi-Fi endpoint or Wi-Fi enabled gateway for Particle Mesh networks. It is based on the Nordic nRF52840 and has built-in battery charging circuitry so it’s easy to connect a Li-Po and deploy your local network in minutes. The Argon is great for connecting existing projects to the Particle Device Cloud or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
